// Digital circuit KolyuzhnyiDZ1.dig as structural Verilog
module KolyuzhnyiDZ1 (
  input  y1,
  input  y2,
  input  y3
);

  wire and_1_out, and_2_out, and_3_out, and_4_out, and_5_out, and_6_out, and_7_out, and_8_out, and_9_out,
       and_10_out, and_11_out, and_12_out, and_13_out, or_1_out, or_2_out, or_3_out, or_4_out, or_5_out,
       or_6_out, or_7_out;

  and and_1 (and_1_out, ~y2, ~y3);  // And
  and and_2 (and_2_out, ~y3, ~y1);  // And
  and and_3 (and_3_out, ~y2, ~y3);  // And
  and and_4 (and_4_out, y1, ~y2);  // And
  and and_5 (and_5_out, ~y1, y2, y3);  // And
  and and_6 (and_6_out, y3, ~y1);  // And
  and and_7 (and_7_out, y1, ~y2, ~y3);  // And
  and and_8 (and_8_out, ~y1, y2, ~y3);  // And
  and and_9 (and_9_out, ~y1, y3);  // And
  and and_10 (and_10_out, ~y1, ~y3);  // And
  and and_11 (and_11_out, ~y2, y3);  // And
  and and_12 (and_12_out, ~y1, y3);  // And
  and and_13 (and_13_out, ~y1, ~y2);  // And
  or or_1 (or_1_out, and_3_out, and_4_out, and_5_out);
  or or_2 (or_2_out, ~y2, and_6_out);  // Or
  or or_3 (or_3_out, and_7_out, and_8_out, and_9_out);
  or or_4 (or_4_out, ~y2, ~y1);  // Or
  or or_5 (or_5_out, ~y2, and_10_out);  // Or
  or or_6 (or_6_out, and_11_out, and_12_out, and_13_out);
  or or_7 (or_7_out, and_1_out, and_2_out);
  Seven_Seg seven_seg_1 (
    .a(or_7_out), .b(or_1_out), .c(or_2_out), .d(or_3_out), .e(or_4_out), .f(or_5_out), .g(or_6_out),
    .dp(1'b0));

  // Notes on the sheet:
  //   с
  //   a
  //   b
  //   d
  //   e
  //   f
  //   g
endmodule
